# Fritzing sketch diyDrumPads (saved by Fritzing 0.7.10b)
breadboards: 1

parts:
  IC1 = IC, DIP package, 20 pins [chip_label=IC part_number="MiCo — atTiny2313 USB-MIDI interface"]
  Nano1 = Arduino Nano v2.3
  R1 = Resistor [tolerance=±5% resistance=220 package=THT]
  XTAL1 = Crystal [frequency="16 Mhz" part_number=12Mhz package=THT]
  CONN1 = USB connector [package=THT]
  R2 = Resistor [tolerance=±5% resistance=100k package=THT]
  R3 = Resistor [tolerance=±5% resistance=100k package=THT]
  R4 = Resistor [tolerance=±5% resistance=100k package=THT]
  R5 = Resistor [tolerance=±5% resistance=100k package=THT]
  D1 = Rectifier Diode [part_number=1N4001 package="300 mil [THT]"]
  J1 = Piezo Speaker
  J2 = Piezo Speaker
  J3 = Piezo Speaker
  J4 = Piezo Speaker
  D2 = Rectifier Diode [part_number=1N4001 package="300 mil [THT]"]
  D3 = Rectifier Diode [part_number=1N4001 package="300 mil [THT]"]
  D4 = Rectifier Diode [part_number=1N4001 package="300 mil [THT]"]

nets:
  N1: IC1.pin2, Nano1.D1TX
  N2: IC1.pin4, XTAL1.pin_0
  N3: IC1.pin5, XTAL1.pin_1
  N4: IC1.pin6, CONN1.d+
  N5: IC1.pin7, R1.Pin_0, CONN1.d-
  N6: IC1.pin10, CONN1.GND, CONN1.chassis5, CONN1.chassis6
  N7: IC1.pin20, Nano1.3V3
  N8: Nano1.GND, R2.Pin_0, R3.Pin_0, R4.Pin_0, R5.Pin_0, D1.anode, J1.pin1, J2.pin1, J3.pin1, J4.pin1, D2.anode, D3.anode, D4.anode
  N9: Nano1.A3, R5.Pin_1, J4.pin2, D4.cathode
  N10: Nano1.A2, R4.Pin_1, J3.pin2, D3.cathode
  N11: Nano1.A1, R3.Pin_1, J2.pin2, D2.cathode
  N12: Nano1.A0, R2.Pin_1, D1.cathode, J1.pin2
  N13: R1.Pin_1, CONN1.5V
